// Logisim project Full Adder Circuit.circ as structural Verilog: 2 circuits, main circuit main
module main (
  input  A,
  input  B,
  input  Carry_In,
  output Carry_Out,
  output Sum
);

  wire A1_out, A2_out, A4_out, I1_out, I2_out, I3_out, I4_out, O2_out, O3_out, O4_out, O5_out;

  not I1 (I1_out, A);
  not I2 (I2_out, B);
  and A1 (A1_out, A, B);
  or O2 (O2_out, A, B);
  or O3 (O3_out, I1_out, I2_out);
  and A2 (A2_out, O2_out, O3_out);
  not I3 (I3_out, A2_out);
  not I4 (I4_out, Carry_In);
  or O4 (O4_out, A2_out, Carry_In);
  or O5 (O5_out, I3_out, I4_out);
  and A4 (A4_out, A2_out, Carry_In);
  or O1 (Carry_Out, A1_out, A4_out);
  and A3 (Sum, O4_out, O5_out);
endmodule

module main__XOR_GATE (
  input  A,
  input  B,
  input  CarryIn,
  output CarryOut,
  output Sum
);

  wire A1_out, A2_out, X1_out;

  and A1 (A1_out, A, B);
  xor X1 (X1_out, A, B);
  xor X2 (Sum, X1_out, CarryIn);
  and A2 (A2_out, X1_out, CarryIn);
  or O1 (CarryOut, A1_out, A2_out);
endmodule
